# Fritzing sketch vegimeter2 (saved by Fritzing 0.8.3b)
circuit board: 15cm x 9cm
breadboards: 3

parts:
  Primary = Power plug
  XBEE = XBee
  LR_5_0V = SPX29302 [part_number=SPX29300T-L-5-0 package=q5-dd_spx29300]
  LR_3_3V = Voltage Regulator - 3.3V [part_number=LM7833 package="TO220 [THT]"]
  Propeller1 = Parallax Propeller D40 [package="DIP [THT]"]
  Pump = Power plug
  Heater = Power plug
  Heater_Relay = RELAY [package=relay-jzc]
  Pump_Relay = RELAY [package=relay-jzc]
  R1 = Resistor [tolerance=±5% resistance=10k package=THT]
  5_MHz_XTAL = CRYSTAL [package=hc49us]
  R2 = Resistor [tolerance=±5% resistance=10k package=THT]
  XBEE_In = LEDs [package=led10mm]
  USB_RX = LEDs [package=led10mm]
  USB_TX = LEDs [package=led10mm]
  Water_A_Temp = Header 3 [package=screwterminal-3.5mm-3_lock.007s]
  Soil_A_Temp = Header 3 [package=screwterminal-3.5mm-3_lock.007s]
  Soil_B_Temp = Header 3 [package=screwterminal-3.5mm-3_lock.007s]
  Soil_C_Temp = Header 3 [package=screwterminal-3.5mm-3_lock.007s]
  Soil_D_Temp = Header 3 [package=screwterminal-3.5mm-3_lock.007s]
  Air_Temp = TEMPERATURE-SENSOR [part_number=DS18B20 package=to-92]
  R3 = Resistor [tolerance=±5% resistance=10k package=THT]
  R4 = Resistor [tolerance=±5% resistance=4.7k package=THT]
  R5 = Resistor [tolerance=±5% resistance=4.7k package=THT]
  R6 = Resistor [tolerance=±5% resistance=4.7k package=THT]
  R7 = Resistor [tolerance=±5% resistance=4.7k package=THT]
  R8 = Resistor [tolerance=±5% resistance=4.7k package=THT]
  R9 = Resistor [tolerance=±5% resistance=4.7k package=THT]
  R11 = Resistor [tolerance=±5% resistance=1k package=THT]
  R12 = Resistor [tolerance=±5% resistance=220 package=THT]
  R13 = Resistor [tolerance=±5% resistance=220 package=THT]
  R14 = Resistor [tolerance=±5% resistance=100 package=THT]
  C3_(4_7uF) = Capacitor [package=cap-pth-small2]
  0_1_uF = Capacitor [package=cap-pth-small2]
  C2_(10_nF) = Capacitor [package=cap-pth-small2]
  ULN2803A = ULN2803A [package=THT]
  XBEE_Out = LEDs [package=led10mm]
  Reset = SWITCH-MOMENTARY-2 [package=tactile_switch_tall]
  FT232RL = USB UART [package=ssop28db]
  Mini_USB = USB Connectors [package=usb-b-pth]
  EEPROM = 24LC256 [package=THT]
  R15 = Resistor [tolerance=±5% resistance=10k package=THT]
  NPN = NPN-Transistor [package="TO92 [THT]"]
  Water_B_Temp = Header 3 [package=screwterminal-3.5mm-3_lock.007s]
  R16 = Resistor [tolerance=±5% resistance=4.7k package=THT]

nets:
  GND: Primary.GND, XBEE.GND, LR_5_0V.GND, LR_3_3V.GND, Propeller1.VSS, Propeller1.BOEn, Heater_Relay.COIL2, Heater_Relay.MAIN, Pump_Relay.COIL2, Pump_Relay.MAIN, Water_A_Temp.1, Soil_A_Temp.1, Soil_B_Temp.1, Soil_C_Temp.1, Soil_D_Temp.1, Air_Temp.GND, R3.Pin_1, C3_(4_7uF).2, 0_1_uF.1, ULN2803A.0V, Reset.2, FT232RL.GND7, FT232RL.GND18, FT232RL.TEST, Mini_USB.GND, EEPROM.A0, EEPROM.A1, EEPROM.A2, EEPROM.0V, EEPROM.WP_-_Write_Protect, NPN.E, Water_B_Temp.1
  VCC: Primary.VCC, LR_5_0V.VIN, LR_3_3V.input_voltage, Heater.VCC
  VCC_2: XBEE.VCC, LR_3_3V.output_voltage, Propeller1.VDD, R1.Pin_1, XBEE_In.A, Water_A_Temp.3, Soil_A_Temp.3, Soil_B_Temp.3, Soil_C_Temp.3, Soil_D_Temp.3, Air_Temp.VCC, R4.Pin_0, R5.Pin_0, R6.Pin_0, R7.Pin_0, R8.Pin_0, R9.Pin_0, XBEE_Out.A, EEPROM.+V, R15.Pin_1, Water_B_Temp.3, R16.Pin_0
  N1: XBEE.pin2, Propeller1.P9, R12.Pin_1
  N2: XBEE.pin3, Propeller1.P8, R13.Pin_1
  N3: LR_5_0V.VOUT, ULN2803A.COM_-_Common
  N4: LR_5_0V.ADJUST, Pump.VCC
  N5: Propeller1.P0, Air_Temp.ADJ, R6.Pin_1
  N6: Propeller1.P1, Water_A_Temp.2, R7.Pin_1
  N7: Propeller1.P2, Soil_A_Temp.2, R5.Pin_1
  N8: Propeller1.P3, Soil_B_Temp.2, R8.Pin_1
  N9: Propeller1.P4, Soil_C_Temp.2, R4.Pin_1
  N10: Propeller1.P5, Soil_D_Temp.2, R9.Pin_1
  N11: Propeller1.P6, R11.Pin_0
  N12: Propeller1.P7, R2.Pin_0
  N13: Propeller1.RESn, Reset.1, NPN.C
  N14: Propeller1.P10, Water_B_Temp.2, R16.Pin_1
  N15: Propeller1.XI, 5_MHz_XTAL.2
  N16: Propeller1.XO, 5_MHz_XTAL.1
  N17: Propeller1.P28, EEPROM.SCL_-_I2C_Clock
  N18: Propeller1.P29, R1.Pin_0, EEPROM.SDA_-_I2C_Data, R15.Pin_0
  N19: Propeller1.P30, FT232RL.RXD
  N20: Propeller1.P31, FT232RL.TXD
  N21: Pump.GND, Pump_Relay.NO
  N22: Heater.GND, Heater_Relay.NO
  N23: Heater_Relay.COIL1, ULN2803A.Out_3, ULN2803A.Out_2
  N24: Pump_Relay.COIL1, ULN2803A.Out_5, ULN2803A.Out_4
  N25: R2.Pin_1, ULN2803A.In_4, ULN2803A.In_5
  N26: XBEE_In.C, R13.Pin_0
  N27: USB_RX.A, USB_TX.A, R14.Pin_0
  N28: USB_RX.C, FT232RL.RXLED
  N29: USB_TX.C, FT232RL.TXLED
  N30: R3.Pin_0, C2_(10_nF).2, NPN.B
  N31: R11.Pin_1, ULN2803A.In_2, ULN2803A.In_3
  N32: R12.Pin_0, XBEE_Out.C
  N33: R14.Pin_1, C3_(4_7uF).1
  N34: 0_1_uF.2, FT232RL.VCCIO, FT232RL.3V3OUT
  N35: C2_(10_nF).1, FT232RL.DTR
  N36: FT232RL.USBDP, Mini_USB.D+
  N37: FT232RL.USBDM, Mini_USB.D-
  N38: FT232RL.VCC, Mini_USB.VBUS

notes:
  Vegimeter 2
  Rev 0
  www.bionicbunny.org
